# Fritzing sketch schema (saved by Fritzing 0.9.1b)
breadboards: 1

parts:
  BeagleBone1 = BeagleBone Black
  J1 = Basic Servo
  M1 = DC Motor
  U1 = ESP8266 WiFi Module [part_number=ESP8266]
  U2 = LIPO-1000mAh [package=lipo-1000]
  U3 = Voltage Regulator [package=to220-adj]
  R1 = Resistor [tolerance=±5% resistance=270 package="1206 [SMD]"]
  D1 = Schottky Diode [part_number=1N5817 package="Melf DO-213 AB [SMD]"]
  C1 = Electrolytic Capacitor [capacitance=2.2mF voltage=20V package="100 mil [THT, electrolytic]"]
  C2 = Electrolytic Capacitor [capacitance=22µF voltage=20V package="100 mil [THT, electrolytic]"]
  R2 = Resistor [tolerance=±5% resistance=1k package="1206 [SMD]"]
  C3 = Electrolytic Capacitor [capacitance=22µF voltage=20V package="100 mil [THT, electrolytic]"]
  D2 = Schottky Diode [part_number=1N5817 package="Melf DO-213 AB [SMD]"]
  C4 = Ceramic Capacitor [capacitance=10nF package="100 mil [THT, multilayer]"]
  IC1 = Modelcraft 207368 [package=soicn]

nets:
  N1: BeagleBone1.no_name_yet#1, U1.GND
  N2: BeagleBone1.no_name_yet#3, U1.VCC
  N3: BeagleBone1.no_name_yet#7, J1.vcc
  N4: BeagleBone1.no_name_yet#11, U1.RXD
  N5: BeagleBone1.no_name_yet#13, U1.TXD
  N6: BeagleBone1.no_name_yet#22, J1.pulse
  N7: BeagleBone1.no_name_yet#45, J1.gnd
  N8: M1.pin_1, IC1.GND_OUT
  N9: M1.pin_2, IC1.VDD_OUT
  N10: U2.+, U3.OUT, C1.+, D2.cathode, IC1.VDD_IN
  N11: U2.-, C1.-, C2.-, R2.Pin_1
  N12: U3.ADJ, R1.Pin_0, D1.anode, C2.+, R2.Pin_0
  N13: U3.IN, R1.Pin_1, D1.cathode, C3.+, D2.anode, C4.0
  N14: C3.-, C4.1

notes:
  5 Volt

custom parts:
  BeagleBone Black: BeagleBone Black rev. A5B
  ESP8266 WiFi Module: Generic WiFi Module based on the ESP8266 with onboard PCB antenna and UART communications
  Modelcraft 207368: PWM Motor Driver
